// Logisim project mam816_lab6.circ as structural Verilog: 1 circuit, main circuit main
module main (
);

  wire button_1_out, CLK, clock_1_out, NOT_of_b_out, subtractor_1_bout;
  wire [15:0] Dividend_Rem_q, Divisor_q, or_2_p2, or_2_p3, Quotient_q, shifter_1_out, shifter_2_out,
       subtractor_1_out;

  Clock clock_1 (.out(clock_1_out));
  or or_1 (CLK, clock_1_out, button_1_out);
  Button button_1 (.out(button_1_out));
  Shifter #(.width(16), .shift("lr")) shifter_1 (.in(Divisor_q), .\dist (4'b0001), .out(shifter_1_out));
  Register #(.width(16)) Divisor (.D(shifter_1_out), .Q(Divisor_q), .clk(CLK));  // open: en, clr
  // Probe on Divisor_q
  Subtractor #(.width(16)) subtractor_1 (
    .a(Dividend_Rem_q), .b(Divisor_q), .out(subtractor_1_out), .bout(subtractor_1_bout));  // open: bin
  not not_1 (NOT_of_b_out, subtractor_1_bout);
  Shifter #(.width(16)) shifter_2 (.in(Quotient_q), .\dist (4'b0001), .out(shifter_2_out));
  // OR_Gate #(.width(16)) or_2: pin names not known; wires that end beside it: shifter_2_out, or_2_p2, or_2_p3
  assign or_2_p2 = {{15{1'b0}}, NOT_of_b_out};  // Bit_Extender bit_extender_1
  // Probe on Dividend_Rem_q
  Register #(.width(16)) Dividend_Rem (
    .D(subtractor_1_out), .en(NOT_of_b_out), .Q(Dividend_Rem_q), .clk(CLK));  // open: clr
  Register #(.width(16)) Quotient (.D(or_2_p3), .Q(Quotient_q), .clk(CLK));  // open: en, clr
  // Probe on Quotient_q
endmodule
